# Fritzing sketch ledcube-control (saved by Fritzing 0.8.7b)
circuit board: 8.53956cm x 5.01576cm
perfboards: 1

parts:
  R1 = Resistor [tolerance=±5% resistance=180k package=THT]
  POWER = female pin header, 2 pins [form="♀ (female)"]
  DATA = female pin header, 3 pins [form="♀ (female)"]
  IC1 = IC, DIP package, 24 pins [chip_label=MAX7221]
  Segments = female pin header, 8 pins [form="♀ (female)"]
  Digits = female pin header, 8 pins [form="♀ (female)"]
  C1 = Electrolytic Capacitor [capacitance=1µF package="100 mil [THT, electrolytic]"]
  C2 = Electrolytic Capacitor [capacitance=1µF package="100 mil [THT, electrolytic]"]

nets:
  N1: R1.Pin_0, IC1.pin18
  N2: R1.Pin_1, POWER.pin1, IC1.pin19, C1.+, C2.+
  N3: POWER.pin2, C1.-, C2.-
  N4: DATA.pin1, IC1.pin13
  N5: DATA.pin2, IC1.pin1
  N6: DATA.pin3, IC1.pin12
  N7: IC1.pin2, Digits.pin1
  N8: IC1.pin3, Digits.pin5
  N9: IC1.pin4, IC1.pin9
  N10: IC1.pin5, Digits.pin7
  N11: IC1.pin6, Digits.pin3
  N12: IC1.pin7, Digits.pin4
  N13: IC1.pin8, Digits.pin8
  N14: IC1.pin10, Digits.pin6
  N15: IC1.pin11, Digits.pin2
  N16: IC1.pin14, Segments.pin2
  N17: IC1.pin15, Segments.pin7
  N18: IC1.pin16, Segments.pin3
  N19: IC1.pin17, Segments.pin8
  N20: IC1.pin20, Segments.pin4
  N21: IC1.pin21, Segments.pin6
  N22: IC1.pin22, Segments.pin1
  N23: IC1.pin23, Segments.pin5
